// Logisim project fiscsim.circ as structural Verilog: 1 circuit, main circuit main
module main (
);

  wire and_1_out, and_2_out, clock_1_out, clock_2_out, clock_3_out, decoder_1_out0, decoder_1_out1,
       decoder_1_out2, decoder_1_out3, not_1_out, not_2_out, register_1_q;
  wire [1:1] undriven_3, undriven_4, undriven_5, undriven_6;
  wire [5:0] adder_1_out, d_ff_1_q, multiplexer_1_out, undriven;
  wire [5:1] undriven_2;
  wire [7:0] multiplexer_2_out, multiplexer_3_out, nor_1_out, register_2_q, register_4_q, undriven_7;
  wire [7:7] rom_1_data;

  Multiplexer #(.width(6)) multiplexer_1 (.in0(undriven), .in1(adder_1_out), .out(multiplexer_1_out), .sel(and_1_out));
  Clock clock_1 (.out(clock_1_out));
  D_Flip_Flop d_ff_1 (.D(multiplexer_1_out[0]), .clk(clock_1_out), .Q(d_ff_1_q[0]));  // open: Qn, preset, reset
  Adder #(.width(6)) adder_1 (.a(d_ff_1_q), .b({undriven_2, 1'b1}), .out(adder_1_out));  // open: cin, cout
  ROM #(.addrWidth(6)) rom_1 (.addr(d_ff_1_q), .data({{2{rom_1_data[7]}}, {6{undriven[0]}}}));
  not not_1 (not_1_out, register_1_q);
  and and_1 (and_1_out, and_2_out, not_1_out);
  and and_2 (and_2_out, rom_1_data[7], rom_1_data[7]);
  Register #(.width(1)) register_1 (
    .D(nor_1_out[0]), .en(not_2_out), .clk(clock_2_out), .Q(register_1_q));  // open: clr
  Clock clock_2 (.out(clock_2_out));
  not not_2 (not_2_out, and_2_out);
  Decoder #(.select(2)) decoder_1 (
    .out0(decoder_1_out0), .out1(decoder_1_out1), .out2(decoder_1_out2), .out3(decoder_1_out3),
    .sel({undriven_3[1], undriven[0]}), .en(not_2_out));
  Clock clock_3 (.out(clock_3_out));
  Register register_2 (.D(undriven_7), .en(decoder_1_out0), .clk(clock_3_out), .Q(register_2_q));  // open: clr
  Register register_3 (.D(undriven_7), .en(decoder_1_out1), .clk(clock_3_out), .Q(register_2_q));  // open: clr
  Register register_4 (.D(undriven_7), .en(decoder_1_out2), .clk(clock_3_out), .Q(register_4_q));  // open: clr
  Register register_5 (.D(undriven_7), .en(decoder_1_out3), .clk(clock_3_out), .Q(register_4_q));  // open: clr
  Multiplexer #(.select(2), .width(8)) multiplexer_2 (
    .in1(register_2_q), .in2(register_2_q), .in3(register_4_q), .out(multiplexer_2_out),
    .sel({undriven_5[1], undriven[0]}));  // open: in0
  Multiplexer #(.select(2), .width(8)) multiplexer_3 (
    .in1(register_2_q), .in2(register_2_q), .in3(register_4_q), .out(multiplexer_3_out),
    .sel({undriven_6[1], undriven[0]}));  // open: in0
  assign nor_1_out = ~(undriven_7 | undriven_7);  // NOR_Gate nor_1, 8 bits wide
  Hex_Digit_Display hex_digit_display_1 ();  // open: value, dp
  Hex_Digit_Display hex_digit_display_2 ();  // open: value, dp
  Adder adder_2 (.a(multiplexer_2_out), .b(multiplexer_3_out));  // open: out, cin, cout
  Multiplexer #(.select(2), .width(8)) multiplexer_4 (.sel({undriven_4[1], rom_1_data[7]}));  // open: in0, in1, in2, in3, out
  // Pins of 1 and 6 bits meet at {undriven_2, 1'b1}
  // Pins of 1 and 6 bits meet at undriven
  // Pins of 1 and 2 bits meet at {undriven_4[1], rom_1_data[7]}
  // Pins of 1 and 2 bits meet at {undriven_5[1], undriven[0]}
  // Pins of 1 and 2 bits meet at {undriven_6[1], undriven[0]}
  // Pins of 1 and 2 bits meet at {undriven_3[1], undriven[0]}
  // Pins of 1 and 8 bits meet at nor_1_out
  // Pins of 1 and 6 bits meet at multiplexer_1_out
  // Pins of 1 and 6 bits meet at d_ff_1_q
endmodule
