// Logisim project CPU_Lab_3.circ as structural Verilog: 6 circuits, main circuit main
module main (
);

  wire alu_1_cout, alu_1_z, undriven;
  wire [1:0] controlcpu_1_ra0, controlcpu_1_ra1, controlcpu_1_wa0;
  wire [3:0] controlcpu_1_opcodealu;
  wire [7:0] alu_1_c, regfile4x8_1_rd0, regfile4x8_1_rd1;
  wire [11:0] rom_1_data;
  wire [12:0] controlcpu_1_addr13b;

  ROM #(.addrWidth(13), .dataWidth(12)) rom_1 (.addr(controlcpu_1_addr13b), .data(rom_1_data));
  RAM ram_1 ();  // open: addr, we, oe, clk, din, dout
  Clock clock_1 ();  // open: out
  ControlCPU controlcpu_1 (
    .Opcode12b(rom_1_data), .Z(alu_1_z), .COut(alu_1_cout), .RA1(controlcpu_1_ra1), .WA0(controlcpu_1_wa0),
    .RA0(controlcpu_1_ra0), .OpcodeALU(controlcpu_1_opcodealu), .ADDR13b(controlcpu_1_addr13b));  // open: MOV, ST, LD, BNZ, BCS, MVI
  RegFile4x8 regfile4x8_1 (
    .WD0(alu_1_c), .WA0(controlcpu_1_wa0), .RA0(controlcpu_1_ra0), .RA1(controlcpu_1_ra1),
    .RD0(regfile4x8_1_rd0), .RD1(regfile4x8_1_rd1));  // open: Enable
  ALU alu_1 (
    .a(regfile4x8_1_rd0), .b(regfile4x8_1_rd1), .opcodeALU(controlcpu_1_opcodealu), .Direction(undriven),
    .z(alu_1_z), .c(alu_1_c), .cout(alu_1_cout));  // open: Shift
endmodule

module FourBitCLA (
  input  cin,
  input  [3:0] a03,
  input  [3:0] b03,
  output [3:0] s03,
  output cout
);

  wire and_1_out, and_2_out, and_3_out, and_4_out, nand_1_out, nand_2_out, nand_3_out, nand_4_out,
       nand_5_out, nand_6_out, nand_7_out, nand_8_out, nand_9_out, nand_10_out, nand_11_out, nand_12_out,
       nand_13_out, not_1_out, not_2_out, not_3_out, not_4_out, xor_1_out, xor_2_out, xor_3_out, xor_4_out;

  and and_1 (and_1_out, a03[0], b03[0]);
  xor xor_1 (xor_1_out, a03[0], b03[0]);
  and and_2 (and_2_out, a03[1], b03[1]);
  xor xor_2 (xor_2_out, a03[1], b03[1]);
  and and_3 (and_3_out, a03[2], b03[2]);
  xor xor_3 (xor_3_out, a03[2], b03[2]);
  and and_4 (and_4_out, a03[3], b03[3]);
  xor xor_4 (xor_4_out, a03[3], b03[3]);
  xor xor_5 (s03[0], xor_1_out, cin);
  xor xor_6 (s03[1], xor_2_out, nand_11_out);
  xor xor_7 (s03[2], xor_3_out, nand_12_out);
  xor xor_8 (s03[3], xor_4_out, nand_13_out);
  not not_1 (not_1_out, and_1_out);
  not not_2 (not_2_out, and_2_out);
  nand nand_1 (nand_1_out, and_1_out, xor_2_out);
  nand nand_2 (nand_2_out, cin, xor_1_out, xor_2_out);
  not not_3 (not_3_out, and_3_out);
  nand nand_3 (nand_3_out, and_2_out, xor_3_out);
  nand nand_4 (nand_4_out, and_1_out, xor_2_out, xor_3_out);
  nand nand_5 (nand_5_out, cin, xor_1_out, xor_2_out, xor_3_out);
  nand nand_6 (nand_6_out, xor_4_out, and_3_out);
  nand nand_7 (nand_7_out, xor_4_out, xor_3_out, and_2_out);
  nand nand_8 (nand_8_out, xor_4_out, xor_3_out, xor_2_out, and_1_out);
  nand nand_9 (nand_9_out, xor_4_out, xor_3_out, xor_2_out, xor_1_out, cin);
  nand nand_10 (nand_10_out, xor_1_out, cin);
  not not_4 (not_4_out, and_4_out);
  nand nand_11 (nand_11_out, not_1_out, nand_10_out);
  nand nand_12 (nand_12_out, not_2_out, nand_1_out, nand_2_out);
  nand nand_13 (nand_13_out, not_3_out, nand_3_out, nand_4_out, nand_5_out);
  nand nand_14 (cout, not_4_out, nand_6_out, nand_7_out, nand_8_out, nand_9_out);
endmodule

module ALU (
  input  [7:0] a,
  input  Shift,
  input  [7:0] b,
  input  [3:0] opcodeALU,
  input  Direction,
  output z,
  output [7:0] c,
  output cout
);

  wire and_1_out, and_3_out, and_4_out, and_6_out, and_7_out, and_8_out, and_9_out, and_10_out, and_11_out,
       and_12_out, and_13_out, and_15_out, decoder_1_out1, fourbitcla_1_cout, not_2_out;
  wire [7:0] and_2_out, and_5_out, demultiplexer_1_out0, demultiplexer_1_out1, fourbitcla_2_s03,
       multiplexer_1_out, not_1_out, not_3_out, or_2_out;

  Demultiplexer #(.width(8)) demultiplexer_1 (
    .out0(demultiplexer_1_out0), .out1(demultiplexer_1_out1), .in(a), .sel(Shift));
  assign not_1_out = ~b;  // NOT_Gate not_1, 8 bits wide
  Decoder #(.select(4)) decoder_1 (
    .out1(decoder_1_out1), .sel(opcodeALU));  // open: out0, out2, out3, out4, out5, out6, out7, out8, out9, out10, out11, out12, out13, out14, out15, en
  not not_2 (not_2_out, Direction);
  Multiplexer #(.width(8)) multiplexer_1 (.in0(b), .in1(not_1_out), .out(multiplexer_1_out), .sel(decoder_1_out1));
  and and_1 (and_1_out, demultiplexer_1_out1[0], Direction);
  and and_2 (and_2_out[0], not_2_out, demultiplexer_1_out1[1]);
  or or_1 (and_2_out[1], and_1_out, and_4_out);
  assign not_3_out = ~demultiplexer_1_out0;  // NOT_Gate not_3, 8 bits wide
  and and_3 (and_3_out, demultiplexer_1_out1[1], Direction);
  and and_4 (and_4_out, not_2_out, demultiplexer_1_out1[2]);
  assign and_5_out = demultiplexer_1_out0 & multiplexer_1_out;  // AND_Gate and_5, 8 bits wide
  assign or_2_out = demultiplexer_1_out0 | multiplexer_1_out;  // OR_Gate or_2, 8 bits wide
  and and_6 (and_6_out, demultiplexer_1_out1[2], Direction);
  or or_3 (and_2_out[2], and_3_out, and_7_out);
  and and_7 (and_7_out, not_2_out, demultiplexer_1_out1[3]);
  and and_8 (and_8_out, demultiplexer_1_out1[3], Direction);
  or or_4 (and_2_out[3], and_6_out, and_9_out);
  and and_9 (and_9_out, not_2_out, demultiplexer_1_out1[4]);
  FourBitCLA fourbitcla_1 (
    .cin(decoder_1_out1), .a03(demultiplexer_1_out0[3:0]), .b03(multiplexer_1_out[3:0]),
    .s03(fourbitcla_2_s03[3:0]), .cout(fourbitcla_1_cout));
  FourBitCLA fourbitcla_2 (
    .cin(fourbitcla_1_cout), .a03(demultiplexer_1_out0[7:4]), .b03(multiplexer_1_out[7:4]),
    .s03(fourbitcla_2_s03[7:4]), .cout(cout));
  and and_10 (and_10_out, demultiplexer_1_out1[4], Direction);
  or or_5 (and_2_out[4], and_8_out, and_11_out);
  and and_11 (and_11_out, not_2_out, demultiplexer_1_out1[5]);
  or or_6 (and_2_out[5], and_10_out, and_13_out);
  and and_12 (and_12_out, demultiplexer_1_out1[5], Direction);
  and and_13 (and_13_out, not_2_out, demultiplexer_1_out1[6]);
  and and_14 (and_2_out[7], demultiplexer_1_out1[6], Direction);
  or or_7 (and_2_out[6], and_12_out, and_15_out);
  Multiplexer #(.select(3), .width(8)) multiplexer_2 (
    .in0(fourbitcla_2_s03), .in1(fourbitcla_2_s03), .in2(and_5_out), .in3(or_2_out), .in4(not_3_out),
    .in5(and_2_out), .in6(and_2_out), .out(c), .sel(opcodeALU[2:0]));  // open: in7
  and and_15 (and_15_out, not_2_out, demultiplexer_1_out1[7]);
  nor nor_1 (z, c[0], c[1], c[2], c[3], c[4], c[5], c[6], c[7]);
endmodule

module RegFile4x8 (
  input  [7:0] WD0,
  input  [1:0] WA0,
  input  [1:0] RA0,
  input  Enable,
  input  [1:0] RA1,
  output [7:0] RD0,
  output [7:0] RD1
);

  wire clock_1_out, decoder_1_out0, decoder_1_out1, decoder_1_out2, decoder_1_out3;
  wire [7:0] register_1_q, register_2_q, register_3_q, register_4_q;

  Decoder #(.select(2)) decoder_1 (
    .out0(decoder_1_out0), .out1(decoder_1_out1), .out2(decoder_1_out2), .out3(decoder_1_out3), .sel(WA0),
    .en(Enable));
  Register register_1 (.D(WD0), .en(decoder_1_out0), .clk(clock_1_out), .Q(register_1_q));  // open: clr
  Register register_2 (.D(WD0), .en(decoder_1_out1), .clk(clock_1_out), .Q(register_2_q));  // open: clr
  Register register_3 (.D(WD0), .en(decoder_1_out2), .clk(clock_1_out), .Q(register_3_q));  // open: clr
  Register register_4 (.D(WD0), .en(decoder_1_out3), .clk(clock_1_out), .Q(register_4_q));  // open: clr
  Clock clock_1 (.out(clock_1_out));
  Multiplexer #(.select(2), .width(8)) multiplexer_1 (
    .in0(register_1_q), .in1(register_2_q), .in2(register_3_q), .in3(register_4_q), .out(RD0), .sel(RA0));
  Multiplexer #(.select(2), .width(8)) multiplexer_2 (
    .in0(register_1_q), .in1(register_2_q), .in2(register_3_q), .in3(register_4_q), .out(RD1), .sel(RA1));
endmodule

module DisplayDecoder (
  input  [2:0] a,
  output [6:0] b
);

  wire and_1_out, and_2_out, and_3_out, and_4_out, and_5_out, and_6_out, and_7_out, and_8_out, and_9_out,
       and_10_out, and_11_out, and_12_out, and_13_out, and_14_out, and_15_out, and_16_out, not_1_out,
       not_2_out, not_3_out;

  not not_1 (not_1_out, a[2]);
  not not_2 (not_2_out, a[1]);
  not not_3 (not_3_out, a[0]);
  and and_1 (and_1_out, not_1_out, not_3_out);
  and and_2 (and_2_out, a[2], a[0]);
  and and_3 (and_3_out, not_2_out, not_3_out);
  and and_4 (and_4_out, a[1], a[0]);
  or or_1 (b[4], not_2_out, a[0], a[2]);
  and and_5 (and_5_out, not_1_out, not_3_out);
  and and_6 (and_6_out, not_1_out, a[1]);
  and and_7 (and_7_out, a[2], not_2_out, a[0]);
  and and_8 (and_8_out, a[1], not_3_out);
  and and_9 (and_9_out, not_1_out, not_3_out);
  and and_10 (and_10_out, a[1], not_3_out);
  and and_11 (and_11_out, not_2_out, not_3_out);
  and and_12 (and_12_out, a[2], not_2_out);
  and and_13 (and_13_out, a[2], not_3_out);
  and and_14 (and_14_out, not_1_out, a[1]);
  and and_15 (and_15_out, a[2], not_2_out);
  and and_16 (and_16_out, a[1], not_3_out);
  or or_2 (b[6], and_1_out, a[1], and_2_out);
  or or_3 (b[5], not_1_out, and_3_out, and_4_out);
  or or_4 (b[3], and_5_out, and_6_out, and_7_out, and_8_out);
  or or_5 (b[2], and_9_out, and_10_out);
  or or_6 (b[1], and_11_out, and_12_out, and_13_out);
  or or_7 (b[0], and_14_out, and_15_out, and_16_out);
  _7_Segment_Display u_7_segment_display_1 (
    .g(b[0]), .f(b[1]), .a(b[6]), .b(b[5]), .e(b[2]), .d(b[3]), .c(b[4]));  // open: dp
endmodule

module ControlCPU (
  input  [11:0] Opcode12b,
  input  Z,
  input  COut,
  output [1:0] RA1,
  output [1:0] WA0,
  output [1:0] RA0,
  output [3:0] OpcodeALU,
  output MOV,
  output ST,
  output LD,
  output [12:0] ADDR13b,
  output BNZ,
  output BCS,
  output MVI
);

  wire and_1_out, clock_1_out, clock_2_out, not_1_out, or_1_out, xor_1_out;
  wire [1:0] Status_q;
  wire [12:0] adder_1_out, multiplexer_1_out;

  Clock clock_1 (.out(clock_1_out));
  not not_1 (not_1_out, Status_q[0]);
  Register #(.width(2)) Status (.D({COut, Z}), .clk(clock_1_out), .Q(Status_q));  // open: en, clr
  xor xor_1 (xor_1_out, Opcode12b[10], Opcode12b[11]);
  or or_1 (or_1_out, not_1_out, Status_q[1]);
  Multiplexer #(.width(13)) multiplexer_1 (
    .in0(13'h1), .in1({{4{Opcode12b[9]}}, Opcode12b[8:0]}), .out(multiplexer_1_out), .sel(and_1_out));
  and and_1 (and_1_out, xor_1_out, or_1_out);
  Adder #(.width(13)) adder_1 (.a(ADDR13b), .b(multiplexer_1_out), .out(adder_1_out));  // open: cin, cout
  and and_2 (BNZ, Opcode12b[10], xor_1_out);
  and and_3 (BCS, Opcode12b[11], xor_1_out);
  and and_4 (MVI, Opcode12b[10], Opcode12b[11]);
  Register #(.width(13)) register_1 (.D(adder_1_out), .en(1'b1), .clk(clock_2_out), .Q(ADDR13b));  // open: clr
  Clock clock_2 (.out(clock_2_out));
  Decoder #(.select(4)) decoder_1 (
    .out8(MOV), .out12(ST), .out13(LD), .sel(Opcode12b[9:6]));  // open: out0, out1, out2, out3, out4, out5, out6, out7, out9, out10, out11, out14, out15, en

  assign OpcodeALU = Opcode12b[9:6];
  assign RA0 = Opcode12b[5:4];
  assign RA1 = Opcode12b[3:2];
  assign WA0 = Opcode12b[1:0];
endmodule
